// Logisim project Controleur.circ as structural Verilog
module main (
  input  [15:0] Instructions,
  input  Clock,
  input  Reset,
  output [7:0] Program_Counter,
  output _0_Load__1_Store,
  output [3:0] Codop_de_l_ALU,
  output [2:0] Registre_Rm,
  output [2:0] Registre_Rd,
  output [2:0] Registre_Rn,
  output [7:0] Immediat_sur_8_bits,
  output [4:0] Imm5
);

  wire _00xxxx, and_1_out, nand_2_out;

  nand nand_1 (_00xxxx, Instructions[15], Instructions[14]);
  nand nand_2 (nand_2_out, Instructions[11], Instructions[12], Instructions[13]);
  and and_1 (and_1_out, nand_2_out, _00xxxx);

  assign Imm5 = Instructions[10:6];
  assign Registre_Rd = Instructions[2:0];
  assign Registre_Rm = Instructions[5:3];

  // Other names for the same wires on the sheet: Clk = Clock; Codop[3:0] = Codop_de_l_ALU; I_6 = Instructions[6];
  //   Instr[15:0] = Instructions; I_7 = Instructions[7]; I_8 = Instructions[8]; I_9 = Instructions[9];
  //   I_10 = Instructions[10]; Imm8[7:0] = Immediat_sur_8_bits; I_11 = Instructions[11]; I_12 = Instructions[12];
  //   I_13 = Instructions[13]; I_14 = Instructions[14]; I_15 = Instructions[15]; Load_Store = _0_Load__1_Store;
  //   PC[7:0] = Program_Counter; I_0 = Instructions[0]; Rd[2:0] = Instructions[2:0]; I_1 = Instructions[1];
  //   I_2 = Instructions[2]; I_3 = Instructions[3]; Rm[2:0] = Instructions[5:3]; I_4 = Instructions[4];
  //   I_5 = Instructions[5]; Rn[2:0] = Registre_Rn

  // Notes on the sheet:
  //   INPUTS
  //   OUTPUTS
endmodule

module Controller (
  input  [15:0] Instructions,
  input  Clock,
  input  Reset,
  output [7:0] Program_Counter,
  output _0_Load__1_Store,
  output [3:0] Codop_de_l_ALU,
  output [2:0] Registre_Rm,
  output [2:0] Registre_Rd,
  output [2:0] Registre_Rn,
  output [7:0] Immediat_sur_8_bits,
  output [4:0] Imm5
);

  wire ADC, AND, and_5_out, ASR, BIC, CMN, CMP, CMP_out, DATA_PROCESSING_out, EOR, LSL, LSR, MOV_out, MUL,
       MVN, nand_1_out, nand_2_out, nand_3_out, nand_4_out, nand_5_out, or_1_out, or_2_out, or_3_out,
       or_5_out, or_6_out, ORR, ROR, RSB, SBC, TST;
  wire [1:1] LSL_out, LSR_out;
  wire [2:0] _5_REG_0, _5_REG_CMP, _5_REG_MOV, and_1_out, and_2_out, and_4_out, and_10_out, and_12_out,
       and_13_out, and_14_out, and_15_out, and_16_out, and_17_out, and_18_out, and_19_out, and_20_out,
       and_21_out, DataProc1, DataProc2, DataProc3, DataProc4, DataProc5;
  wire [2:2] ASR_out;
  wire [3:0] _5_CodeOp, and_7_out, and_8_out, and_9_out, and_11_out, bit_extender_7_out, or_4_out;
  wire [4:0] _5_IMM_5, and_3_out;
  wire [7:0] _5_IMM_8, and_6_out;

  nand u_LSL (LSL_out[1], Instructions[11], Instructions[12], Instructions[13], Instructions[14], Instructions[15]);
  and u_LSR (LSR_out[1], Instructions[11], nand_1_out);
  assign and_1_out = Instructions[5:3] & _5_REG_0;  // AND_Gate and_1, 3 bits wide
  assign and_2_out = Instructions[2:0] & _5_REG_0;  // AND_Gate and_2, 3 bits wide
  nand nand_1 (nand_1_out, Instructions[11], Instructions[12], Instructions[13], Instructions[14]);
  and u_ASR (ASR_out[2], Instructions[12], nand_2_out);
  assign and_3_out = Instructions[10:6] & _5_IMM_5;  // AND_Gate and_3, 5 bits wide
  nand nand_2 (nand_2_out, Instructions[11], Instructions[13], Instructions[14], Instructions[15]);
  nand nand_3 (nand_3_out, Instructions[11], Instructions[12], Instructions[14], Instructions[15]);
  and MOV (MOV_out, Instructions[13], nand_3_out);
  assign and_4_out = Instructions[10:8] & _5_REG_MOV;  // AND_Gate and_4, 3 bits wide
  and and_5 (and_5_out, Instructions[13], Instructions[11]);
  nand nand_4 (nand_4_out, Instructions[12], Instructions[14], Instructions[15]);
  and u_CMP (CMP_out, and_5_out, nand_4_out);
  or or_1 (or_1_out, CMP_out, MOV_out);
  assign and_6_out = Instructions[7:0] & _5_IMM_8;  // AND_Gate and_6, 8 bits wide
  assign _5_REG_0 = {{2{or_2_out}}, or_2_out};  // Bit_Extender bit_extender_1
  or or_2 (or_2_out, LSL_out[1], LSR_out[1], ASR_out[2]);
  assign _5_IMM_5 = {{4{or_2_out}}, or_2_out};  // Bit_Extender bit_extender_2
  assign _5_IMM_8 = {{7{or_1_out}}, or_1_out};  // Bit_Extender bit_extender_3
  assign _5_REG_MOV = {{2{MOV_out}}, MOV_out};  // Bit_Extender bit_extender_4
  assign _5_REG_CMP = {{2{CMP_out}}, CMP_out};  // Bit_Extender bit_extender_5
  or or_3 (or_3_out, LSL_out[1], LSR_out[1], ASR_out[2]);
  assign _5_CodeOp = {{3{or_3_out}}, or_3_out};  // Bit_Extender bit_extender_6
  assign and_7_out = {2'b00, LSL_out[1], 1'b0} & _5_CodeOp;  // AND_Gate and_7, 4 bits wide
  assign and_8_out = {2'b00, {2{LSR_out[1]}}} & _5_CodeOp;  // AND_Gate and_8, 4 bits wide
  assign and_9_out = {1'b0, ASR_out[2], 2'b00} & _5_CodeOp;  // AND_Gate and_9, 4 bits wide
  assign or_4_out = and_7_out | and_8_out | and_9_out;  // OR_Gate or_4, 4 bits wide
  assign and_10_out = Instructions[10:8] & _5_REG_CMP;  // AND_Gate and_10, 3 bits wide
  nand nand_5 (nand_5_out, Instructions[10], Instructions[11], Instructions[12], Instructions[13], Instructions[14], Instructions[15]);
  and DATA_PROCESSING (DATA_PROCESSING_out, Instructions[14], nand_5_out);
  assign bit_extender_7_out = {{3{DATA_PROCESSING_out}}, DATA_PROCESSING_out};  // Bit_Extender bit_extender_7
  assign and_11_out = Instructions[9:6] & bit_extender_7_out;  // AND_Gate and_11, 4 bits wide
  Decoder_part #(.select(4)) decoder_1 (
    .out0(AND), .out1(EOR), .out2(LSL), .out3(LSR), .out4(ASR), .out5(ADC), .out6(SBC), .out7(ROR),
    .out8(TST), .out9(RSB), .out10(CMP), .out11(CMN), .out12(ORR), .out13(MUL), .out14(BIC), .out15(MVN),
    .sel(and_11_out));  // open: en
  assign and_12_out = {Instructions[3], Instructions[4], Instructions[5]} & DataProc1;  // AND_Gate and_12, 3 bits wide
  assign and_13_out = {Instructions[0], Instructions[1], Instructions[2]} & DataProc1;  // AND_Gate and_13, 3 bits wide
  assign and_14_out = {Instructions[3], Instructions[4], Instructions[5]} & DataProc2;  // AND_Gate and_14, 3 bits wide
  assign and_15_out = {Instructions[0], Instructions[1], Instructions[2]} & DataProc2;  // AND_Gate and_15, 3 bits wide
  assign and_16_out = {Instructions[3], Instructions[4], Instructions[5]} & DataProc3;  // AND_Gate and_16, 3 bits wide
  assign and_17_out = {Instructions[0], Instructions[1], Instructions[2]} & DataProc3;  // AND_Gate and_17, 3 bits wide
  assign and_18_out = {Instructions[3], Instructions[4], Instructions[5]} & DataProc4;  // AND_Gate and_18, 3 bits wide
  assign and_19_out = {Instructions[0], Instructions[1], Instructions[2]} & DataProc4;  // AND_Gate and_19, 3 bits wide
  or or_5 (or_5_out, AND, EOR, LSL, LSR, ASR, ADC, SBC, ROR, ORR, MVN);
  or or_6 (or_6_out, CMP, CMN);
  assign and_20_out = {Instructions[3], Instructions[4], Instructions[5]} & DataProc4;  // AND_Gate and_20, 3 bits wide
  assign and_21_out = {Instructions[0], Instructions[1], Instructions[2]} & DataProc4;  // AND_Gate and_21, 3 bits wide
  assign DataProc1 = {{2{or_5_out}}, or_5_out};  // Bit_Extender bit_extender_8
  assign DataProc2 = {{2{TST}}, TST};  // Bit_Extender bit_extender_9
  assign DataProc3 = {{2{RSB}}, RSB};  // Bit_Extender bit_extender_10
  assign DataProc4 = {{2{or_6_out}}, or_6_out};  // Bit_Extender bit_extender_11
  assign DataProc5 = {{2{MUL}}, MUL};  // Bit_Extender bit_extender_12
  assign Registre_Rm = and_1_out | and_12_out | and_14_out | and_20_out;  // OR_Gate or_7, 3 bits wide
  assign Registre_Rd = and_2_out | and_4_out | and_13_out | and_17_out | and_19_out | and_21_out;  // OR_Gate or_8, 3 bits wide
  assign Registre_Rn = and_10_out | and_15_out | and_16_out | and_18_out;  // OR_Gate or_9, 3 bits wide
  assign Imm5 = and_3_out;  // OR_Gate or_10, 5 bits wide OR_Gate
  assign Immediat_sur_8_bits = and_6_out;  // OR_Gate or_11, 8 bits wide OR_Gate
  assign Codop_de_l_ALU = or_4_out | and_11_out;  // OR_Gate or_12, 4 bits wide

  // Other names for the same wires on the sheet: I_10 = Instructions[10]; Instr[15:0] = Instructions;
  //   I_6 = Instructions[6]; I_7 = Instructions[7]; I_8 = Instructions[8]; I_9 = Instructions[9];
  //   I_5 = Instructions[5]; I_4 = Instructions[4]; I_3 = Instructions[3]; I_2 = Instructions[2];
  //   I_1 = Instructions[1]; I_0 = Instructions[0]; Clk = Clock; Codop[3:0] = Codop_de_l_ALU;
  //   Imm8[7:0] = Immediat_sur_8_bits; I_11 = Instructions[11]; I_12 = Instructions[12]; I_13 = Instructions[13];
  //   I_14 = Instructions[14]; I_15 = Instructions[15]; Load_Store = _0_Load__1_Store; PC[7:0] = Program_Counter;
  //   Rd[2:0] = Registre_Rd; Rm[2:0] = Registre_Rm; Rn[2:0] = Registre_Rn

  // Notes on the sheet:
  //   INPUTS
  //   OUTPUTS
  //   5-Bits CodeOp
  //   6-Bits CodeOp
  //   Ca doit etre Rdn -->
  //   Ca doit etre Rd -->
  //   Ca doit etre Rdm -->
  //   Ca doit etre Rd -->
endmodule
