// Logisim project Projet_PEP.circ as structural Verilog: 1 circuit, main circuit main
module main (
  input  CarryIn,
  input  [4:0] Shifter,
  input  [3:0] CodeOp,
  input  [31:0] DataIn,
  input  in_5,
  input  [2:0] RegDest,
  input  [2:0] RegA,
  input  [2:0] RegB,
  output [3:0] Flags
);

  wire clock_1_out;
  wire [31:0] alu_32_bits_1_out_6, main_1_aout, main_1_bout, multiplexer_1_out;

  Clock clock_1 (.out(clock_1_out));
  Multiplexer #(.width(32), .enable("false")) multiplexer_1 (
    .in0(alu_32_bits_1_out_6), .in1(DataIn), .out(multiplexer_1_out), .sel(in_5));
  Banc_registre_main main_1 (
    .DataIn(multiplexer_1_out), .RegtDest(RegDest), .RegA(RegA), .RegB(RegB), .Clk(clock_1_out),
    .Aout(main_1_aout), .Bout(main_1_bout));  // open: Reset
  ALU_32_Bits alu_32_bits_1 (
    .CarryIn(CarryIn), .A(main_1_aout), .B(main_1_bout), .CodeOp(CodeOp), .Shifter(Shifter), .Flags(Flags),
    .out_6(alu_32_bits_1_out_6));
  // Probe on alu_32_bits_1_out_6
endmodule
