// Logisim project Projet_PEP.circ as structural Verilog: 1 circuit, main circuit main
module main (
  input  CarryIn,
  input  Clr,
  input  Sel,
  input  Ld,
  input  Reset,
  input  in_6
);

  wire Clk;
  wire [2:0] controller_1_registre_rd, controller_1_registre_rm, controller_1_registre_rn;
  wire [3:0] alu_32_bits_1_p3, controller_1_codop_de_l_alu;
  wire [4:0] controller_1_imm5;
  wire [7:0] controller_1_immediat_sur_8_bits, controller_1_program_counter;
  wire [15:0] rom_1_inst;
  wire [31:0] alu_32_bits_1_p6, banc_registre_1_aout, banc_registre_1_bout, multiplexer_1_out, ram_1_dataout;

  ROM rom_1 (.Addres(controller_1_program_counter), .Inst(rom_1_inst));  // open: sel
  Controller controller_1 (
    .Instructions(rom_1_inst), .Clock(Clk), .Reset(Reset), .Flags(alu_32_bits_1_p3),
    .Program_Counter(controller_1_program_counter), ._0_Load__1_Store(Ld),
    .Codop_de_l_ALU(controller_1_codop_de_l_alu), .Registre_Rm(controller_1_registre_rm),
    .Registre_Rd(controller_1_registre_rd), .Registre_Rn(controller_1_registre_rn),
    .Immediat_sur_8_bits(controller_1_immediat_sur_8_bits), .Imm5(controller_1_imm5));
  Clock Clock (.out(Clk));
  Multiplexer #(.width(32), .enable("false")) multiplexer_1 (
    .in0(alu_32_bits_1_p6), .in1(ram_1_dataout), .out(multiplexer_1_out), .sel(in_6));
  Banc_Registre banc_registre_1 (
    .DataIn(multiplexer_1_out), .RegtDest(controller_1_registre_rd), .RegA(controller_1_registre_rm),
    .RegB(controller_1_registre_rn), .Clk(Clk), .Reset(Reset), .Aout(banc_registre_1_aout),
    .Bout(banc_registre_1_bout));
  // ALU_32_Bits alu_32_bits_1: pin names not known; wires that end beside it: controller_1_imm5, controller_1_codop_de_l_alu, alu_32_bits_1_p3, banc_registre_1_bout, banc_registre_1_aout, alu_32_bits_1_p6, CarryIn
  RAM ram_1 (
    .Address(controller_1_immediat_sur_8_bits), .Datain(alu_32_bits_1_p6), .sel(Clk), .Clk(Sel), .Ld(Ld),
    .Clr(Clr), .Dataout(ram_1_dataout));

  // Other names for the same wires on the sheet: Res = Reset
endmodule
